# Fritzing sketch Multifactor authentication Sketch (saved by Fritzing 0.9.4)
circuit board: 11.4278cm x 7.87015cm

parts:
  Mod1 = sensor_biometrico
  U4 = G3VM-61E1 [package=g3vm-61e1]
  LCD2 = LCD screen
  LCM1602_IIC1 = LCM1602 IIC [part_number="LCM1602 IIC" chip_label="LCM1602 IIC" package="DIP (Dual Inline) [THT]"]
  Part2 = Arduino Board Ethernet
  U5 = RFID RC522 SIP - 8 pins [chip_label="RFID RC522" package="SIP (Single Inline) [THT]"]
  U6 = DC 5V TO ± 12V Mini DC converter [package=THT]
  Keypad4x1 = Keypad Membran 4x4
  BAT1 = Battery Holders [package=lipo-1100mAh]
  L2 = Solenoid
  J1 = Piezo Speaker

nets:
  VCC: Mod1.VCC, Part2.5V
  N1: Mod1.TX, Part2.A0
  N2: Mod1.RX, Part2.A1
  GND: Mod1.GND, U4.P$4, LCM1602_IIC1.GND, Part2.GND, U5.GND, U6.GND, J1.pin1
  N3: U4.P$2, U6.-12V, BAT1.+
  N4: U4.P$5, Part2.A3
  VIN: U4.P$6, LCM1602_IIC1.VCC, Part2.VIN, U6.Vin
  VSS: LCD2.VSS, LCM1602_IIC1.VSS
  VDD: LCD2.VDD, LCM1602_IIC1.VDD
  N5: LCD2.V0, LCM1602_IIC1.V0
  N6: LCD2.RS, LCM1602_IIC1.RS
  N7: LCD2.R/W, LCM1602_IIC1.RW
  N8: LCD2.E, LCM1602_IIC1.E
  N9: LCD2.DB0, LCM1602_IIC1.D0
  N10: LCD2.DB1, LCM1602_IIC1.D1
  N11: LCD2.DB2, LCM1602_IIC1.D2
  N12: LCD2.DB3, LCM1602_IIC1.D3
  N13: LCD2.DB4, LCM1602_IIC1.D4
  N14: LCD2.DB5, LCM1602_IIC1.D5
  N15: LCD2.DB6, LCM1602_IIC1.D6
  N16: LCD2.DB7, LCM1602_IIC1.D7
  N17: LCD2.LED+, LCM1602_IIC1.A
  N18: LCD2.LED-, LCM1602_IIC1.K
  N19: LCM1602_IIC1.SDA, Part2.A4
  N20: LCM1602_IIC1.SCL, Part2.A5
  N21: Part2.D8, Keypad4x1.Pin2
  N22: Part2.D9_PWM, Keypad4x1.Pin1
  N23: Part2.D10_PWM/SS, U5.NSS
  N24: Part2.D11/MOSI, U5.MOSI
  N25: Part2.D12/MISO, U5.MISO
  N26: Part2.D13/SCK, U5.SCK
  N27: Part2.A2, J1.pin2
  N28: Part2.D0/RX, U5.RST
  N29: Part2.D2_PWM, Keypad4x1.Pin8
  N30: Part2.D3_PWM, Keypad4x1.Pin7
  N31: Part2.D4, Keypad4x1.Pin6
  N32: Part2.D5_PWM, Keypad4x1.Pin5
  N33: Part2.D6_PWM, Keypad4x1.Pin4
  N34: Part2.D7, Keypad4x1.Pin3
  3V3: Part2.3V3, U5.VCC
  N35: U6.+12V, BAT1.-, L2.pin1

notes:
  RElay
  [wkghjgjgjhghjghjghjgjjhjhg note here]

custom parts:
  sensor_biometrico: Adafruit Optical Fingerprint Sensor
  LCM1602 IIC: I2C-Module to use a 1602 or 2004 LCD on with the wire.h libory Serial LCD Modul
  RFID RC522 SIP - 8 pins: A SIP stand-in part for RFID RC522 . With 8 pins on a 300 mil single inline package (SIP) footprint.
  DC 5V TO ± 12V Mini DC converter: DC 5V TO ± 12V Mini DC converter from ebay (search for "DC 5V TO ± 12V Mini DC converter"). Supplies ± 12V at up to 30MA output for op amps or rs232 drivers from a 3 to 5V input (so a battery or 3.3 or 5V power rail) on a micro).
  Keypad Membran 4x4: Membrane Keypad 4x4 Matrix
